// Logisim project arm.circ as structural Verilog
module main (
  input  [7:0] in_1,
  input  [7:0] in_2,
  input  in_3,
  input  [7:0] in_4,
  input  [7:0] in_5,
  input  in_6,
  input  [31:0] in_7,
  input  [4:0] in_8,
  output [7:0] out_9,
  output [7:0] out_10,
  output [7:0] out_11,
  output [7:0] out_12,
  output [7:0] out_13,
  output out_14,
  output ZERO,
  output SIGN,
  output [7:0] RESULT,
  output CARRY,
  output OVERFLOW,
  output [7:0] out_20,
  output out_21,
  output [31:0] out_22
);

  wire adder_2_cout;
  wire [7:0] multiplexer_1_out, negator_1_out;
  wire [9:9] shifter_1_out;

  Negator negator_1 (.in(in_5), .out(negator_1_out));
  Multiplexer #(.width(8), .enable("false")) multiplexer_1 (
    .in0(in_5), .in1(negator_1_out), .out(multiplexer_1_out), .sel(in_6));
  Shifter #(.width(10), .shift("rr")) shifter_1 (
    .in({in_3, in_4, 1'b0}), .\dist (4'b0001), .out({shifter_1_out[9], out_20, out_21}));
  Adder adder_1 (.a(in_4), .b(multiplexer_1_out), .out(RESULT), .cin(in_3), .cout(CARRY));
  Shifter #(.width(32), .shift("rr")) shifter_2 (.in(in_7), .\dist (in_8), .out(out_22));
  Divider divider_1 (.a(in_4), .b(in_5), .out(out_9), .upper(in_1), .rem(out_10));
  Multiplier multiplier_1 (.a(in_4), .b(in_5), .out(out_11), .cin(in_2), .cout(out_12));
  Subtractor subtractor_1 (.a(in_4), .b(in_5), .out(out_13), .bout(out_14));  // open: bin
  Adder #(.width(7)) adder_2 (.a(in_4[6:0]), .b(multiplexer_1_out[6:0]), .cin(in_3), .cout(adder_2_cout));  // open: out
  xor xor_1 (OVERFLOW, CARRY, adder_2_cout);
  Comparator comparator_1 (.a(RESULT), .b({8{1'b0}}), .eq(ZERO));  // open: gt, lt

  assign SIGN = RESULT[7];
endmodule

module prefetch (
  input  in_1,
  input  PC_WRT,
  output [15:0] out_3
);

  wire and_1_out, and_2_out, clock_1_out, counter_1_q, decoder_1_out0, decoder_1_out1, decoder_2_out0,
       decoder_2_out1, not_1_out;
  wire [15:0] adder_1_out, IR0_q, IR1_q, PC_q, ram_1_data;

  Clock clock_1 (.out(clock_1_out));
  Counter #(.width(1), .max('h1)) counter_1 (
    .count(in_1), .Q(counter_1_q), .clk(clock_1_out));  // open: load, D, carry, clr
  Decoder #(.enable("false")) decoder_1 (.out0(decoder_1_out0), .out1(decoder_1_out1), .sel(counter_1_q));
  and and_1 (and_1_out, in_1, decoder_1_out1);
  Adder #(.width(16)) adder_1 (.a(PC_q), .b(16'h1), .out(adder_1_out));  // open: cin, cout
  and and_2 (and_2_out, in_1, decoder_1_out0);
  Register #(.width(16)) PC (.D(adder_1_out), .en(PC_WRT), .Q(PC_q), .clk(clock_1_out));  // open: clr
  Register #(.width(16)) IR0 (.D(ram_1_data), .en(and_2_out), .Q(IR0_q), .clk(clock_1_out));  // open: clr
  Register #(.width(16)) IR1 (.D(ram_1_data), .en(and_1_out), .Q(IR1_q), .clk(clock_1_out));  // open: clr
  not not_1 (not_1_out, counter_1_q);
  Decoder #(.enable("false")) decoder_2 (.out0(decoder_2_out0), .out1(decoder_2_out1), .sel(not_1_out));
  Multiplexer #(.width(16), .enable("false")) multiplexer_1 (.in0(IR0_q), .in1(IR1_q), .out(out_3), .sel(not_1_out));
  RAM #(.addrWidth(16), .dataWidth(16)) ram_1 (
    .addr(PC_q), .data(ram_1_data), .clk(clock_1_out));  // open: sel, ld, clr
endmodule
