// Logisim project clock1.circ as structural Verilog: 1 circuit, main circuit main
module main (
  input  in_1,
  input  [3:0] in_2,
  input  in_3,
  input  [3:0] in_4
);

  wire and_1_out, clock_1_out, controlled_buffer_1_out, counter_1_carry, counter_2_carry, not_1_out,
       not_2_out, not_3_out, or_1_out;
  wire [3:0] counter_1_q, counter_2_q;

  Clock clock_1 (.out(clock_1_out));
  assign controlled_buffer_1_out = or_1_out ? clock_1_out : 1'bz;  // Controlled_Buffer controlled_buffer_1
  or or_1 (or_1_out, counter_2_carry, not_3_out);
  not not_1 (not_1_out, counter_2_carry);
  and and_1 (and_1_out, clock_1_out, not_1_out, counter_1_carry);
  not not_2 (not_2_out, controlled_buffer_1_out);
  // Probe on counter_1_q
  Counter #(.width(4), .max('hf)) counter_1 (
    .load(in_1), .D(in_2), .Q(counter_1_q), .carry(counter_1_carry), .clk(controlled_buffer_1_out));  // open: count, clr
  // Probe on counter_2_q
  Counter #(.width(4), .max('hf)) counter_2 (
    .load(in_3), .D(in_4), .Q(counter_2_q), .carry(counter_2_carry), .clk(and_1_out));  // open: count, clr
  LED led_1 (.in(controlled_buffer_1_out));
  LED led_2 (.in(not_2_out));
  LED led_3 (.in(counter_1_carry));
  not not_3 (not_3_out, counter_1_carry);
  LED led_4 (.in(counter_2_carry));
  DotMatrix #(.matrixcols(1), .matrixrows(4)) dotmatrix_1 (.col0(counter_1_q));
  DotMatrix #(.matrixcols(1), .matrixrows(4)) dotmatrix_2 (.col0(counter_2_q));
endmodule
