// Logisim project reg3.circ as structural Verilog: 1 circuit, main circuit main
module main (
  input  cnt_out,
  input  r0_out,
  input  r1_out,
  input  r0_enbl,
  input  r1_enbl,
  input  mem_in,
  input  rand_out,
  input  mem_out,
  input  mem_enbl,
  input  mem_load,
  input  addr_lo_enbl,
  input  addr_hi_enbl,
  input  in_13,
  input  pc_rst
);

  wire clk_out;
  wire [3:0] adr_lo_2_q, adr_lo_q, controlled_buffer_1_out, controlled_buffer_5_out, counter_1_q, r0_q, r1_q,
       random_1_out;
  wire [7:0] adder_1_out, bit_extender_1_out, register_1_q;
  wire [15:0] buffer_1_out, rom_1_data;

  Clock clk (.out(clk_out));
  assign bit_extender_1_out = {{7{1'b0}}, 1'b1};  // Bit_Extender bit_extender_1
  // Probe on controlled_buffer_1_out
  Adder adder_1 (.a(register_1_q), .b(bit_extender_1_out), .out(adder_1_out));  // open: cin, cout
  Hex_Digit_Display hex_digit_display_1 (.value(controlled_buffer_1_out));  // open: dp
  Register #(.width(4)) r0 (.D(controlled_buffer_1_out), .en(r0_enbl), .Q(r0_q), .clk(clk_out));  // open: clr
  Register #(.width(4)) r1 (.D(controlled_buffer_1_out), .en(r1_enbl), .Q(r1_q), .clk(clk_out));  // open: clr
  // Probe on adder_1_out
  assign controlled_buffer_1_out = r0_out ? r0_q : 4'bz;  // Controlled_Buffer controlled_buffer_1
  assign controlled_buffer_1_out = r1_out ? r1_q : 4'bz;  // Controlled_Buffer controlled_buffer_2
  Random #(.width(4)) random_1 (.clk(clk_out), .out(random_1_out));  // open: next, clr
  // Probe on register_1_q
  Register register_1 (.D(adder_1_out), .en(in_13), .Q(register_1_q), .clk(clk_out), .clr(buffer_1_out[0]));
  assign controlled_buffer_1_out = buffer_1_out[1] ? random_1_out : 4'bz;  // Controlled_Buffer controlled_buffer_3
  Register #(.width(4)) adr_lo (
    .D(controlled_buffer_1_out), .en(addr_lo_enbl), .Q(adr_lo_q), .clk(clk_out));  // open: clr
  Register #(.width(4)) adr_lo_2 (
    .D(controlled_buffer_1_out), .en(addr_hi_enbl), .Q(adr_lo_2_q), .clk(clk_out));  // open: clr
  ROM #(.dataWidth(16)) rom_1 (.addr(register_1_q), .data(rom_1_data));  // open: sel
  Counter #(.width(4), .max('hf)) counter_1 (.Q(counter_1_q), .clk(clk_out));  // open: load, D, count, carry, clr
  // Probe on rom_1_data
  assign controlled_buffer_1_out = cnt_out ? counter_1_q : 4'bz;  // Controlled_Buffer controlled_buffer_4
  assign buffer_1_out = rom_1_data;  // Buffer buffer_1, 16 bits wide
  assign controlled_buffer_5_out = mem_in ? controlled_buffer_1_out : 4'bz;  // Controlled_Buffer controlled_buffer_5
  // Probe on controlled_buffer_5_out
  assign controlled_buffer_1_out = mem_out ? controlled_buffer_5_out : 4'bz;  // Controlled_Buffer controlled_buffer_6
  RAM #(.dataWidth(4)) ram_1 (
    .addr({adr_lo_2_q, adr_lo_q}), .data(controlled_buffer_5_out), .sel(mem_enbl), .clk(clk_out),
    .ld(mem_load));  // open: clr

  // Notes on the sheet:
  //   contents of rom_1 (hex, n*v repeats v):
  //   2 1
endmodule
